# Fritzing sketch breadboard002 (saved by Fritzing 0.9.2b)
breadboards: 1

parts:
  U1 = ESP8266 NodeMCU LoLin module
  Q1 = npn-Powertransistor [package="TO220 [THT]"]
  Q2 = npn-Powertransistor [package="TO220 [THT]"]
  Q3 = npn-Powertransistor [package="TO220 [THT]"]
  R1 = Resistor [tolerance=±5% resistance=220 package="2512 [SMD]"]
  R2 = Resistor [tolerance=±5% resistance=220 package="2512 [SMD]"]
  R3 = Resistor [tolerance=±5% resistance=220 package="2512 [SMD]"]
  LED1 = RGB LED (com. cathode, rgb) [package="5 mm [THT]"]
  U2 = LMZ14203 [package=to-pmod-7]
  Power_plug1 = Power plug
  R4 = Resistor [tolerance=±5% resistance=220 package="2512 [SMD]"]
  R5 = Resistor [tolerance=±5% resistance=220 package="2512 [SMD]"]
  R6 = Resistor [tolerance=±5% resistance=220 package="2512 [SMD]"]
  LED2 = RGB LED (com. cathode, rgb) [package="5 mm [THT]"]

nets:
  N1: U1.D1, R1.Pin_1
  N2: U1.D2, R2.Pin_1
  N3: U1.D4, R3.Pin_1
  GND: U1.GND, Q1.emitter, Q2.emitter, Q3.emitter, U2.GND, Power_plug1.GND, LED2.common_cathode
  N4: U1.D6, R4.Pin_1
  N5: U1.D7, R5.Pin_1
  N6: U1.D8, R6.Pin_1
  N7: U1.Vin, U2.VOUT
  N8: Q1.base, R3.Pin_0
  N9: Q1.collector, LED1.blue_anode
  N10: Q2.base, R2.Pin_0
  N11: Q2.collector, LED1.green_anode
  N12: Q3.base, R1.Pin_0
  N13: Q3.collector, LED1.red_anode
  VIN: LED1.common_cathode, U2.VIN, Power_plug1.VCC
  N14: R4.Pin_0, LED2.red_anode
  N15: R5.Pin_0, LED2.green_anode
  N16: R6.Pin_0, LED2.blue_anode

notes:
  Status
  LED
  to RGB Strip
  12V 3A
  VIn
  1K
  8V Voltage
  Regulator

custom parts:
  ESP8266 NodeMCU LoLin module: ESP8266 based NodeMCU
